# Fritzing sketch astros-viewer (saved by Fritzing 1.0.6)
breadboards: 1

parts:
  Part2 = Arduino Mega 2560 (Rev3)
  U1 = LCD-16X2 [package=lcd-16x2_noholes]
  R1 = Resistor [tolerance=±5% power=0.25W resistance=220 package=THT]
  R2 = Resistor [tolerance=±5% resistance=220 package="0603 [SMD]"]
  R3 = Resistor [tolerance=±5% resistance=330k package="0603 [SMD]"]
  LED2 = LEDs [package=led10mm]
  R4 = Resistor [tolerance=±5% power=0.25W resistance=220 package=THT]
  R5 = Resistor [tolerance=±5% power=0.25W resistance=220 package=THT]
  R6 = Resistor [tolerance=±5% power=0.25W resistance=220 package=THT]
  LED3 = LEDs [package=led10mm]
  LED4 = LEDs [package=led10mm]
  LED5 = LEDs [package=led10mm]
  R7 = Resistor [tolerance=±5% power=0.25W resistance=220 package=THT]
  R8 = Resistor [tolerance=±5% power=0.25W resistance=220 package=THT]
  R9 = Resistor [tolerance=±5% power=0.25W resistance=220 package=THT]
  R10 = Resistor [tolerance=±5% power=0.25W resistance=220 package=THT]
  R11 = Resistor [tolerance=±5% power=0.25W resistance=220 package=THT]
  R12 = Resistor [tolerance=±5% power=0.25W resistance=220 package=THT]
  LED6 = LEDs [package=led10mm]
  LED7 = LEDs [package=led10mm]
  LED8 = LEDs [package=led10mm]
  LED9 = LEDs [package=led10mm]
  LED10 = LEDs [package=led10mm]
  LED11 = LEDs [package=led10mm]
  8x8_LED_Modul_mit_MAX1 = 8x8 LED Modul mit MAX7219 [package=THT]

nets:
  N1: Part2.D13_PWM, U1.DB7
  N2: Part2.D12_PWM, U1.DB6
  N3: Part2.D11_PWM, U1.DB5
  N4: Part2.D10_PWM, U1.DB4
  N5: Part2.D9_PWM, U1.E
  N6: Part2.D8_PWM, U1.RS
  5V: Part2.5V, U1.VDD, U1.A, R3.Pin_1, 8x8_LED_Modul_mit_MAX1.VCC_Eingang
  N7: Part2.GND, R2.Pin_1, LED2.C, LED3.C, LED5.C, LED7.C, LED8.C, LED9.C, LED10.C, LED11.C
  N8: Part2.D40, R1.Pin_0
  N9: Part2.D41, R4.Pin_0
  N10: Part2.D42, R5.Pin_0
  N11: Part2.D43, R6.Pin_0
  N12: Part2.D44, R7.Pin_0
  N13: Part2.D45, R9.Pin_0
  N14: Part2.D46, R8.Pin_0
  N15: Part2.D47, R10.Pin_0
  N16: Part2.D48, R11.Pin_0
  N17: Part2.D49, R12.Pin_0
  N18: Part2.D50, 8x8_LED_Modul_mit_MAX1.DIN_Eingang
  N19: Part2.D52, 8x8_LED_Modul_mit_MAX1.CS_Eingang
  N20: Part2.D53, 8x8_LED_Modul_mit_MAX1.CLK_Eingang
  N21: U1.VSS, U1.R_W, U1.K, 8x8_LED_Modul_mit_MAX1.GND_Eingang
  N22: U1.VO, R2.Pin_0, R3.Pin_0
  N23: R1.Pin_1, LED2.A
  N24: R4.Pin_1, LED3.A
  N25: R5.Pin_1, LED4.A
  N26: R6.Pin_1, LED5.A
  N27: R7.Pin_1, LED6.A
  N28: R8.Pin_1, LED7.A
  N29: R9.Pin_1, LED8.A
  N30: R10.Pin_1, LED9.A
  N31: R11.Pin_1, LED10.A
  N32: R12.Pin_1, LED11.A
